# Fritzing sketch Schematic (saved by Fritzing 0.9.2b)
breadboards: 1

parts:
  Ultrasonic_Sensor = single row smd male pin header, 4 pins [form="♂ (male)"]
  U1 = Optocoupler [package=THT]
  U2 = Optocoupler [package=THT]
  Intel_Edison = female pin header, 5 pins [form="♀ (female)"]
  R1 = Resistor [tolerance=±5% resistance=66 package=THT]
  R2 = Resistor [tolerance=±5% resistance=1k package=THT]
  R3 = Resistor [tolerance=±5% resistance=330 package=THT]
  R4 = Resistor [tolerance=±5% resistance=330 package=THT]

nets:
  5V: Ultrasonic_Sensor.pin1, U1.Pin_5
  N1: Ultrasonic_Sensor.pin2, R3.Pin_0
  N2: Ultrasonic_Sensor.pin3, R4.Pin_0
  GND: Ultrasonic_Sensor.pin4, U2.Pin_2
  N3: U1.Pin_1, R1.Pin_0
  N4: U1.Pin_2, Intel_Edison.pin1
  N5: U1.Pin_4, R3.Pin_1
  N6: U2.Pin_1, R4.Pin_1
  N7: U2.Pin_4, Intel_Edison.pin3
  N8: U2.Pin_5, R2.Pin_0
  N9: Intel_Edison.pin2, R2.Pin_1
  N10: Intel_Edison.pin4, R1.Pin_1

notes:
  Vcc
  Trigger
  Echo
  Gnd
  J19 - pin 3 (Gnd)
  J18 - pin 2 (Input GPIO)
  J18 - pin 1 (Output GPIO)
  J19 - pin 2 (1.8V)
  J20 - pin 2 (3.3V)
